# Fritzing sketch ATINY_bluetooth_sender_receiver (saved by Fritzing 0.9.3b)
breadboards: 1

parts:
  R1 = 100K Ω Resistor [package=THT]
  IC1 = ATINY85 [package=dip08]
  VCC1 = Battery
  LED1 = LED - 5mm [color="Red (633nm)" package="5 mm [THT]"]
  LED2 = LED - 5mm [color="Green (570nm)" package="5 mm [THT]"]
  S1 = Toggle Switch [package=THT]
  HC05BTModule1 = Bluetooth HC-05 Macho  # not connected

nets:
  N1: R1.Pin_0, IC1.A_V-, VCC1.-, LED1.cathode, LED2.cathode, S1.L2
  N2: R1.Pin_1, IC1.B_-IN, S1.COM
  N3: IC1.B_+IN, LED2.anode
  N4: IC1.B_OUT, LED1.anode
  N5: IC1.A_V+, VCC1.+, S1.L1

notes:
  Alarm input received and send
  Alarm input
  1K
  On/ Off command receieved

custom parts:
  100K Ω Resistor: A generic resistor (0.25W)
  ATINY85: Arduino compatibel microcontroller.
